# Fritzing sketch Fritzing Sketch Single Gate (saved by Fritzing 0.9.3b)
breadboards: 1

parts:
  VCC1 = Battery
  Q1 = LTR-301 [package=ltr-301]
  LED1 = LED - 3mm [color="Infrared (940nm)" package="3 mm [THT]"]
  R1 = Resistor [tolerance=±5% resistance=100 package=THT]
  S1 = Toggle Switch [package=THT]
  S2 = Pushbutton [package="[SMD]"]
  Part1 = 0.56" 7-segment LED Backpack
  R2 = Resistor [tolerance=±5% resistance=10k package=THT]
  Part2 = Itsy Bitsy 32u4 3V @ 8MHz [part_number="Adafruit 3675"]

nets:
  N1: VCC1.-, Q1.E, LED1.cathode, Part2.GND
  N2: VCC1.+, S1.COM
  N3: Q1.C, R2.Pin_0, Part2.A0
  N4: LED1.anode, R1.Pin_1
  VDD: R1.Pin_0, S1.L2, Part1.VDD, R2.Pin_1, Part2.+3V3
  N5: S2.Pin_1, S2.Pin_2, Part2.D7
  N6: S2.Pin_3, S2.Pin_4, Part1.GND
  N7: Part1.SCL, Part2.SCL
  N8: Part1.SDA, Part2.SDA

custom parts:
  0.56" 7-segment LED Backpack: This 0.56" 7-segment LED display includes a driver chip for simple control via an I2C interface. The backpack features address-selection jumpers so you can connect up to eight displays on a single I2C bus.
  Itsy Bitsy 32u4 3V @ 8MHz: What's smaller than a Feather but larger than a Trinket? It's an Itsy Bitsy! Small, powerful, Arduino-compatible - this microcontroller board is perfect when you want something very compact, but still with a bunch of pins. Itsy Bitsy is only 1.4" long by 0.7" wide, but has 6 power pins, 6 analog & digital pins and 17 digital pins. It packs much of the same capability as an Arduino UNO or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
