# Fritzing sketch Fritzing Sketch (saved by Fritzing 0.9.3b)
breadboards: 1

parts:
  VCC1 = Battery
  Q1 = LTR-301 [package=ltr-301]
  LED1 = LED - 3mm [color="Infrared (940nm)" package="3 mm [THT]"]
  R1 = Resistor [tolerance=±5% resistance=100 package=THT]
  S1 = Toggle Switch [package=THT]
  S2 = Pushbutton [package="[SMD]"]
  R2 = Resistor [tolerance=±5% resistance=100 package=THT]
  LED2 = LED - 3mm [color="Infrared (940nm)" package="3 mm [THT]"]
  U1 = Itsy Bitsy M0 Express
  Part1 = 0.56" 7-segment LED Backpack
  R4 = Resistor [tolerance=±5% resistance=10k package=THT]
  R3 = Resistor [tolerance=±5% resistance=10k package=THT]
  Q2 = LTR-301 [package=ltr-301]

nets:
  GND: VCC1.-, Q1.E, LED1.cathode, S2.Pin_3, S2.Pin_4, LED2.cathode, U1.GND, Part1.GND, Q2.E
  N1: VCC1.+, S1.COM
  N2: Q1.C, U1.A3, R3.Pin_0
  N3: LED1.anode, R1.Pin_1
  N4: R1.Pin_0, S1.L2, U1.+3V3, R4.Pin_1, R3.Pin_1
  N5: S2.Pin_1, S2.Pin_2, U1.D4
  N6: R2.Pin_0, LED2.anode
  N7: U1.SCL, Part1.SCL
  N8: U1.SDA, Part1.SDA
  N9: U1.A5, R4.Pin_0, Q2.C

notes:
  Note

custom parts:
  Itsy Bitsy M0 Express: What's smaller than a Feather but larger than a Trinket? It's an Adafruit ItsyBitsy M0 Express! Small, powerful, with a rockin' ATSAMD21 Cortex M0 processor running at 48 MHz - this microcontroller board is perfect when you want something very compact, but still with a bunch of pins. ItsyBitsy M0 Express is only 1.4" long by 0.7" wide, but has 6 power pins, 23 digital GPIO pins (12 of which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
  0.56" 7-segment LED Backpack: This 0.56" 7-segment LED display includes a driver chip for simple control via an I2C interface. The backpack features address-selection jumpers so you can connect up to eight displays on a single I2C bus.
