# Fritzing sketch Fritzing Sketch (saved by Fritzing 0.9.3b)
breadboards: 1

parts:
  VCC1 = Battery
  Q1 = LTR-301 [package=ltr-301]
  LED1 = LED - 3mm [color="Infrared (940nm)" package="3 mm [THT]"]
  R1 = Resistor [tolerance=±5% resistance=100 package=THT]
  S1 = Toggle Switch [package=THT]
  S2 = Pushbutton [package="[SMD]"]
  R2 = Resistor [tolerance=±5% resistance=100 package=THT]
  LED2 = LED - 3mm [color="Infrared (940nm)" package="3 mm [THT]"]
  Q2 = LTR-301 [package=ltr-301]
  Part2 = Itsy Bitsy M0 Express
  Part3 = 0.56" 7-segment LED Backpack [part_number=881]

nets:
  GND: VCC1.-, Q1.E, LED1.cathode, S2.Pin_3, S2.Pin_4, LED2.cathode, Q2.E, Part2.GND, Part3.GND
  N1: VCC1.+, S1.COM
  N2: Q1.C, Part2.D9
  N3: LED1.anode, R1.Pin_1
  +3V3: R1.Pin_0, S1.L2, R2.Pin_1, Part2.+3V3, Part3.VDD
  N4: S2.Pin_1, S2.Pin_2, Part2.D4
  N5: R2.Pin_0, LED2.anode
  N6: Q2.C, Part2.D7
  N7: Part2.SCL, Part3.SCL
  N8: Part2.SDA, Part3.SDA

custom parts:
  Itsy Bitsy M0 Express: What's smaller than a Feather but larger than a Trinket? It's an Adafruit ItsyBitsy M0 Express! Small, powerful, with a rockin' ATSAMD21 Cortex M0 processor running at 48 MHz - this microcontroller board is perfect when you want something very compact, but still with a bunch of pins. ItsyBitsy M0 Express is only 1.4" long by 0.7" wide, but has 6 power pins, 23 digital GPIO pins (12 of which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
  0.56" 7-segment LED Backpack: This 0.56" 7-segment LED display includes a driver chip for simple control via an I2C interface. The backpack features address-selection jumpers so you can connect up to eight displays on a single I2C bus.
